# Fritzing sketch arduino (saved by Fritzing 0.9.3b)
breadboards: 1

parts:
  Bauteil1 = Arduino Uno (Rev3)
  Raspberry_Pi_1 = Raspberry Pi 3 [part_number=RPI-3-V1.2]
  U1 = RELAY-SOLIDSTATE [package=relay-s108t02]

nets:
  N1: Bauteil1.D4, Raspberry_Pi_1.GPIO26
  N2: Bauteil1.D7, Raspberry_Pi_1.GPIO19
  N3: Bauteil1.5V, U1.+
  GND: Bauteil1.GND, Raspberry_Pi_1.GND, U1.-
